# Fritzing sketch Smart-Sprayer (saved by Fritzing 0.9.3b)

parts:
  M1 = 1 chan 5v relay module
  M2 = 1 chan 5v relay module
  HC-SR04_Sensor_1 = HC-SR04 Ultrasonic Distance Sensor
  HC-SR04_Sensor_2 = HC-SR04 Ultrasonic Distance Sensor
  GSM_SIM_GPSR_SMS_SIM900_SIM1 = SIM800L [package=THT]
  C1 = Electrolytic Capacitor [capacitance=1000µF package="300 mil [THT, electrolytic]"]
  U4 = LM2596 step down module
  LED1 = LEDs [package=led10mm]
  ZS-042_RTC1 = ZS-042 RTC Module
  S1 = Round Pushbutton
  S2 = Round Pushbutton
  S3 = Round Pushbutton
  LED2 = LEDs [package=led10mm]
  S4 = Round Pushbutton
  HLK-PM1 = HLK-PM12 [part_number=HLK-PM12]
  WATER_PUMP1 = water pump/motor
  WATER_PUMP2 = water pump/motor
  Raspberry_Pi_1 = Raspberry Pi 4 [part_number=RPI-4-b]
  U2 = LM2596 step down module
  J1 = Piezo Speaker

nets:
  VCC: M1.pin_1, M2.pin_1, HC-SR04_Sensor_1.VCC, HC-SR04_Sensor_2.VCC, U2.OUT+
  GND: M1.pin_2, M2.pin_2, HC-SR04_Sensor_1.GND, HC-SR04_Sensor_2.GND, WATER_PUMP1.pin_1, U2.IN-, U2.OUT-
  N1: M1.pin_3, Raspberry_Pi_1.GPIO5
  N2: M1.pin_4, WATER_PUMP2.pin_2
  N3: M1.pin_5, M2.pin_5, U4.IN+, HLK-PM1.+Vo, U2.IN+
  N4: M2.pin_3, Raspberry_Pi_1.GPIO4
  N5: M2.pin_4, WATER_PUMP1.pin_2
  N6: HC-SR04_Sensor_1.TRIG, Raspberry_Pi_1.GPIO19
  N7: HC-SR04_Sensor_1.ECHO, Raspberry_Pi_1.GPIO26
  N8: HC-SR04_Sensor_2.TRIG, Raspberry_Pi_1.GPIO6
  N9: HC-SR04_Sensor_2.ECHO, Raspberry_Pi_1.GPIO13
  5V: GSM_SIM_GPSR_SMS_SIM900_SIM1.5V, GSM_SIM_GPSR_SMS_SIM900_SIM1.VDD, C1.+, U4.OUT+
  N10: GSM_SIM_GPSR_SMS_SIM900_SIM1.GND, C1.-, U4.IN-, U4.OUT-, HLK-PM1.-Vo, WATER_PUMP2.pin_1
  N11: GSM_SIM_GPSR_SMS_SIM900_SIM1.SIM_TXD, Raspberry_Pi_1.GPIO17
  N12: GSM_SIM_GPSR_SMS_SIM900_SIM1.SIM_RXD, Raspberry_Pi_1.GPIO16
  GND_2: LED1.C, ZS-042_RTC1.GND, S1.leg0, S2.leg0, S3.leg0, LED2.C, S4.leg1, Raspberry_Pi_1.GND, J1.pin1
  N13: LED1.A, Raspberry_Pi_1.GPIO21
  VCC_2: ZS-042_RTC1.VCC, Raspberry_Pi_1.3v3
  N14: ZS-042_RTC1.SDA, Raspberry_Pi_1.GPIO2
  N15: ZS-042_RTC1.SCL, Raspberry_Pi_1.GPIO3
  N16: S1.leg1, Raspberry_Pi_1.GPIO18
  N17: S2.leg1, Raspberry_Pi_1.GPIO22
  N18: S3.leg1, Raspberry_Pi_1.GPIO23
  N19: LED2.A, Raspberry_Pi_1.GPIO20
  N20: S4.leg0, Raspberry_Pi_1.GPIO24
  N21: Raspberry_Pi_1.GPIO12, J1.pin2

custom parts:
  1 chan 5v relay module: 1 Channel 5V Relay Module Board Shield with Optocoupler Support High and Low Level Trigger for Arduino.
  LM2596 step down module: LM2596 DC-DC step down power supply module 3 A.
  water pump/motor: WATER PUMP BY ARDUBLOCKTR
  Raspberry Pi 4: The RPi4, a faster version of the awesome Raspberry Pi 2 B ARM Board with 40 pin gpio. Ready for special Raspberry Pi B+ and RPi2 Hat (Hardware attached (on) top)
